# Fritzing sketch circuit_ESP8266_DHT11_DS18B20 (saved by Fritzing 0.9.3b)
breadboards: 1

parts:
  R1 = Resistor [tolerance=±5% resistance=10k package=THT]
  WeMos_D1_R1 = WeMos D1 R2
  DHT11 = DHT11 Humitidy and Temperature Sensor
  DS1 = DS18B20 1-Wire Temperature Sensor [part_number=DS18B20]
  R2 = Resistor [tolerance=±5% resistance=4.7k package="1206 [SMD]"]

nets:
  VDD: R1.Pin_0, WeMos_D1_R1.5V, DHT11.VDD, DS1.VDD, R2.Pin_1
  N1: R1.Pin_1, WeMos_D1_R1.(D5), DHT11.DATA
  N2: WeMos_D1_R1.D2, DS1.DQ, R2.Pin_0
  GND: WeMos_D1_R1.GND, DHT11.GND, DS1.GND

custom parts:
  WeMos D1 R2: The D1 R2 is a mini wifi board based on the ESP-8266EX.
  DHT11 Humitidy and Temperature Sensor: DHT11 Humidity and Temperature Sensor
