# Fritzing sketch circuit_ESP8266_DS18B20 (saved by Fritzing 0.9.3b)
breadboards: 1

parts:
  WeMos_D1_R1 = WeMos D1 R2
  DS1 = DS18B20 1-Wire Temperature Sensor [part_number=DS18B20]
  R1 = Resistor [tolerance=±5% resistance=4.7k package="2512 [SMD]"]

nets:
  N1: WeMos_D1_R1.(D5), DS1.DQ, R1.Pin_0
  GND: WeMos_D1_R1.GND, DS1.GND
  5V: WeMos_D1_R1.5V, DS1.VDD, R1.Pin_1

custom parts:
  WeMos D1 R2: The D1 R2 is a mini wifi board based on the ESP-8266EX.
