# Fritzing sketch circuit (saved by Fritzing 0.9.3b)
breadboards: 2

parts:
  DS1 = DS18B20 1-Wire Temperature Sensor [part_number=DS18B20]
  R1 = Resistor [tolerance=±5% resistance=4.7 package="0402 [SMD]"]
  LCD1 = LCD screen
  Raspberry_Pi_1 = Raspberry Pi 3 [part_number=RPI-3-V1.2]
  R3 = Rotary Potentiometer (Large) [maximum_resistance=10kΩ package=THT]
  R2 = Rotary Potentiometer (Large) [maximum_resistance=10kΩ package=THT]

nets:
  GND: DS1.GND, LCD1.VSS, LCD1.R/W, LCD1.LED-, Raspberry_Pi_1.GND, R3.leg2
  N1: DS1.DQ, R1.Pin_0, Raspberry_Pi_1.GPIO4
  3V3: DS1.VDD, R1.Pin_1, Raspberry_Pi_1.3v3, Raspberry_Pi_1.3V3
  VDD: LCD1.VDD, Raspberry_Pi_1.5V, R2.wiper
  N2: LCD1.V0, R3.wiper
  N3: LCD1.RS, Raspberry_Pi_1.GPIO26
  N4: LCD1.E, Raspberry_Pi_1.GPIO19
  N5: LCD1.DB4, Raspberry_Pi_1.GPIO13
  N6: LCD1.DB5, Raspberry_Pi_1.GPIO6
  N7: LCD1.DB6, Raspberry_Pi_1.GPIO5
  N8: LCD1.DB7, Raspberry_Pi_1.GPIO11
  N9: LCD1.LED+, R2.leg2
